# Fritzing sketch Arduino LCD TMP36 (saved by Fritzing 0.8.3b)
breadboards: 1

parts:
  Parte1 = Arduino Uno (Rev3)
  U1 = LCD-16X2 [package=lcd-16x2]
  T1 = TMP36 Temperature Sensor [package="TO92 [THT]"]

nets:
  N1: Parte1.A0, T1.Vout
  GND: Parte1.GND, U1.A, T1.GND
  N2: Parte1.D11_PWM/MOSI, U1.DB4
  N3: Parte1.D12/MISO, U1.DB6
  N4: Parte1.D2, U1.VO
  N5: Parte1.D3_PWM, U1.RS
  N6: Parte1.D4, U1.R_W
  N7: Parte1.D5_PWM, U1.E
  N8: Parte1.3V3, T1.+Vs
  N9: Parte1.5V, U1.DB5, U1.DB7, U1.K

notes:
  De izquierda (pin 1) a derecha (pin 14)
  PIN
  Descripción
  1
  GND
  2
  +5V/td&gt;
  3
  En principio hay que conectarlo a +5V, pero a través de un potenciómetro. En mi caso concreto, ha funcionado conectado a GND directamente. Regula el brillo de las letras. Es por eso que un valor erróneo en esta patilla hace que no se muestre nada por la pantalla.
  4
  RS (bajo para command, alto para character)
  5
  RW (bajo para escritura, alto para lectura)
  6
  Enable
  7-14
  Pines de datos
  15-16
